# Fritzing sketch 220_Kirchoff_Oomi (saved by Fritzing 0.9.4)
breadboards: 1

parts:
  R1 = Resistor [tolerance=±5% resistance=220 package="1206 [SMD]"]
  R2 = Resistor [tolerance=±5% resistance=220 package="1206 [SMD]"]
  BAT1 = BC9VPC [package=bc9vpc]
  R3 = Resistor [tolerance=±5% resistance=220 package="2010 [SMD]"]

nets:
  N1: R1.Pin_0, BAT1.V+
  N2: R1.Pin_1, R2.Pin_0, R3.Pin_0
  N3: R2.Pin_1, BAT1.V-, R3.Pin_1
