# Fritzing sketch 220_Kirchoff_Oomi_2 (saved by Fritzing 0.9.4)
breadboards: 1

parts:
  R1 = Resistor [tolerance=±5% resistance=220 package="1206 [SMD]"]
  R23 = Resistor [tolerance=±5% resistance=110 package="1206 [SMD]"]
  BAT1 = BC9VPC [package=bc9vpc]

nets:
  N1: R1.Pin_0, BAT1.V+
  N2: R1.Pin_1, R23.Pin_0
  N3: R23.Pin_1, BAT1.V-
