# Fritzing sketch 220_Kirchoff_Oomi_3 (saved by Fritzing 0.9.4)
breadboards: 1

parts:
  R123 = Resistor [tolerance=±10% resistance=330 package="1206 [SMD]"]
  BAT1 = BC9VPC [package=bc9vpc]

nets:
  N1: R123.Pin_0, BAT1.V+
  N2: R123.Pin_1, BAT1.V-
